# Fritzing sketch Ekran Board (saved by Fritzing 0.9.0b)
perfboards: 1

parts:
  JP25 = Header 8 [package=1x08_smd_alt]
  Ekran = Header 8 [package=1x08_smd_alt]
  GND = Header 1 [package=1x01_offset]  # not connected
  JP26 = Header 1 [package=1x01_offset]
  JP27 = Header 1 [package=1x01_offset]
  JP28 = Header 1 [package=1x01_offset]
  JP29 = Header 1 [package=1x01_offset]
  JP30 = Header 1 [package=1x01_offset]
  5V = Header 1 [package=1x01_offset]  # not connected
  JP31 = Header 1 [package=1x01_offset]
  R4 = Rotary Potentiometer (Small) [maximum_resistance=100kΩ package=THT]
  R5 = Resistor [tolerance=±5% resistance=220 package=THT]  # not connected
  JP32 = Header 1 [package=1x01_offset]
  JP33 = Header 1 [package=1x01_offset]
  JP34 = Header 1 [package=1x01_offset]
  LED2 = LED - 5mm [color="Red (633nm)" package="5 mm [THT]"]

nets:
  N1: JP25.3, JP27.1
  N2: JP25.4, JP28.1
  N3: JP25.5, JP30.1
  N4: JP25.6, JP31.1
  N5: Ekran.2, LED2.anode
  N6: Ekran.3, R4.wiper, JP34.1
  N7: Ekran.4, JP29.1
  N8: Ekran.5, R4.leg1, JP32.1
  N9: Ekran.6, JP26.1
  N10: R4.leg2, JP33.1
