# Fritzing sketch LDR Board (saved by Fritzing 0.9.0b)
perfboards: 1

parts:
  R15 = Resistor [tolerance=±5% resistance=100 package=THT]
  5V = Header 1 [package=1x01_offset]
  Transistor = Header 1 [package=1x01_offset]
  Analog = Header 1 [package=1x01_offset]
  GND = Header 1 [package=1x01_offset]
  R16 = Photocell (LDR) [package=THT]
  Q2 = NPN-Transistor [package="TO92 [THT]"]

nets:
  N1: R15.Pin_0, GND.1
  N2: R15.Pin_1, Analog.1, R16.pin_0
  N3: 5V.1, Q2.C
  N4: Transistor.1, Q2.B
  N5: R16.pin_1, Q2.E
