# Fritzing sketch Seven_Segment (saved by Fritzing 0.9.0b)
perfboards: 1

parts:
  DI6 = 7-Segment LED Display [package=THT]  # not connected
  DI7 = 7-Segment LED Display [package=THT]
  R2 = Resistor [tolerance=±5% resistance=100 package=THT]
  JP18 = Header 1 [package=1x01_offset]  # not connected
  JP19 = Header 1 [package=1x01_offset]  # not connected
  JP20 = Header 1 [package=1x01_offset]  # not connected
  JP21 = Header 1 [package=1x01_offset]  # not connected
  JP22 = Header 1 [package=1x01_offset]  # not connected
  JP23 = Header 1 [package=1x01_offset]  # not connected
  JP24 = Header 1 [package=1x01_offset]  # not connected
  JP25 = Header 1 [package=1x01_offset]  # not connected
  JP26 = Header 1 [package=1x01_offset]  # not connected
  JP27 = Header 1 [package=1x01_offset]  # not connected
  JP28 = Header 1 [package=1x01_offset]  # not connected
  JP29 = Header 1 [package=1x01_offset]  # not connected
  JP30 = Header 1 [package=1x01_offset]  # not connected
  JP31 = Header 1 [package=1x01_offset]  # not connected
  JP32 = Header 1 [package=1x01_offset]  # not connected
  JP33 = Header 1 [package=1x01_offset]  # not connected
  JP34 = Header 1 [package=1x01_offset]  # not connected

nets:
  N1: DI7.commAnode, R2.Pin_0
