# Fritzing sketch TCRT5000 Board (saved by Fritzing 0.9.0b)
perfboards: 1

parts:
  R21 = Resistor [tolerance=±5% resistance=10k package=THT]
  R22 = Resistor [tolerance=±5% resistance=100 package=THT]
  5V = Header 1 [package=1x01_offset]
  Transistor = Header 1 [package=1x01_offset]
  Analog = Header 1 [package=1x01_offset]
  GND = Header 1 [package=1x01_offset]
  LED6 = LED - 5mm [color="Red (633nm)" package="5 mm [THT]"]
  R23 = Photocell (LDR) [package=THT]  # not connected
  R24 = Photocell (LDR) [package=THT]
  Q2 = NPN-Transistor [package="TO92 [THT]"]

nets:
  N1: R21.Pin_0, Q2.E
  N2: R21.Pin_1, Analog.1, R24.pin_0
  N3: R22.Pin_1, LED6.cathode
  N4: 5V.1, Q2.C
  N5: Transistor.1, Q2.B
  N6: GND.1, R24.pin_1
