# Fritzing sketch Uzaklık Board (saved by Fritzing 0.9.0b)
perfboards: 1

parts:
  2 = Header 1 [package=1x01_offset]
  JP10 = Header 1 [package=1x01_offset]
  3 = Header 1 [package=1x01_offset]
  JP11 = Header 1 [package=1x01_offset]
  JP12 = Header 1 [package=1x01_offset]
  JP13 = Header 1 [package=1x01_offset]
  3_Sensor = screw terminal, 4 pins
  2_Sensor = screw terminal, 4 pins
  GND = Header 1 [package=1x01_offset]
  5V = Header 1 [package=1x01_offset]
  1_Sensor = screw terminal, 4 pins

nets:
  N1: 2.1, 1_Sensor.pin2
  N2: JP10.1, 3_Sensor.pin2
  N3: 3.1, 3_Sensor.pin1
  N4: JP11.1, 2_Sensor.pin4
  N5: JP12.1, 1_Sensor.pin1
  N6: JP13.1, 2_Sensor.pin3
  N7: 3_Sensor.pin3, GND.1
  N8: 3_Sensor.pin4, 5V.1
