# Fritzing sketch Uzaklık_Sensoru_Atmega (saved by Fritzing 0.9.0b)
breadboards: 1

parts:
  U2 = atmega328 [package=dip]
  C3 = Capacitor [package=cap-pth-small2]
  C4 = Capacitor [package=cap-pth-small2]
  VCC2 = Battery block 9V
  R2 = Resistor [tolerance=±5% resistance=100 package=THT]
  S3 = Pushbutton [package=THT]
  XTAL2 = Crystal [frequency="16 Mhz" package=THT]
  IC2 = Voltage Regulator [package=to-220-alt]

nets:
  N1: U2.RESET, R2.Pin_1, S3.leg0
  N2: U2.D4, R2.Pin_0
  N3: U2.VCC, C3.2, C4.1, S3.leg1
  N4: U2.XLAT1, C3.1, XTAL2.pin_1
  N5: U2.XLAT2, C4.2, XTAL2.pin_0
  N6: VCC2.-, IC2.IN
  N7: VCC2.+, IC2.GND
