# Fritzing sketch Shift Register & 4511 (saved by Fritzing 0.9.0b)
perfboards: 1

parts:
  U8 = 74HC595 [package="DIP16 [THT]"]
  4511 = XR2206 [package=dil16]
  JP38 = Header 1 [package=1x01_offset]
  JP39 = Header 1 [package=1x01_offset]
  JP40 = Header 1 [package=1x01_offset]
  JP41 = Header 1 [package=1x01_offset]
  JP42 = Header 1 [package=1x01_offset]
  JP43 = Header 1 [package=1x01_offset]
  JP44 = Header 1 [package=1x01_offset]
  JP45 = Header 1 [package=1x01_offset]
  JP46 = Header 1 [package=1x01_offset]
  JP47 = Header 1 [package=1x01_offset]
  JP48 = Header 1 [package=1x01_offset]
  JP49 = Header 1 [package=1x01_offset]

nets:
  N1: U8.Q1, 4511.STO
  N2: U8.Q2, 4511.MO
  N3: U8.Q6, 4511.AMSI
  N4: U8.Q7, 4511.SYMA1
  N5: U8.Q7', JP43.1
  N6: U8.MR, JP45.1
  N7: U8.SH_CP, JP44.1
  N8: U8.ST_CP, JP49.1
  N9: U8.OE, JP46.1
  N10: U8.DS, JP47.1
  N11: U8.Q0, JP48.1
  N12: U8.VCC, JP39.1
  N13: 4511.SYNCO, JP40.1
  N14: 4511.GND, JP41.1
  N15: 4511.WAVEA1, JP38.1
  N16: 4511.WAVEA2, JP42.1
