# Fritzing sketch Transistör (saved by Fritzing 0.9.0b)
perfboards: 1

parts:
  Motor_- = Header 1 [package=1x01_offset]  # not connected
  Güç_Girişi = Screw terminal - 2 pins [package=THT]
  Arduino_GND_ve_PWM = Screw terminal - 2 pins [package=THT]
  R2 = Resistor [tolerance=±5% resistance=10k package=THT]  # not connected
  Motor_+ = Header 1 [package=1x01_offset]
  Q2 = Basic FET N-Channel [package="TO220 [THT]"]

nets:
  N1: Güç_Girişi.pin1, Q2.source
  N2: Güç_Girişi.pin2, Motor_+.1
  N3: Arduino_GND_ve_PWM.pin1, Q2.gate
